# Fritzing sketch lcd (saved by Fritzing 0.9.3b)
breadboards: 1

parts:
  Raspberry_Pi_1 = Raspberry Pi 3 [part_number=RPI-3-V1.2]
  U1 = LCD-16X2 [package=lcd-16x2]

nets:
  N1: Raspberry_Pi_1.GIPO4, U1.DB0
  N2: Raspberry_Pi_1.GIPO17, U1.DB1
  N3: Raspberry_Pi_1.GIPO27, U1.DB2
  N4: Raspberry_Pi_1.GIPO22, U1.DB3
  N5: Raspberry_Pi_1.GIPO5, U1.DB4
  N6: Raspberry_Pi_1.GIPO6, U1.DB5
  N7: Raspberry_Pi_1.GIPO13, U1.DB6
  N8: Raspberry_Pi_1.GIPO26, U1.DB7
  N9: Raspberry_Pi_1.GIPO24, U1.E
  N10: Raspberry_Pi_1.GIPO23, U1.R_W
  N11: Raspberry_Pi_1.GIPO18, U1.RS
  GND: Raspberry_Pi_1.GND, U1.VSS, U1.VO, U1.K
  5V: Raspberry_Pi_1.5V, U1.VDD, U1.A
